# Fritzing sketch sunfounderlcd (saved by Fritzing 0.9.3b)

parts:
  Part1 = LCD1602-I2C
  Part2 = Arduino Uno (Rev3)

nets:
  GND: Part1.GND, Part2.GND
  VCC: Part1.VCC, Part2.5V
  N1: Part1.SDA, Part2.A4/SDA
  N2: Part1.SCL, Part2.A5/SCL

custom parts:
  LCD1602-I2C: A standard character display, usually with 2x16 characters. Comes in many colors with LCM1602 IIC attached.
